# Fritzing sketch OXI001 (saved by Fritzing 0.9.3b)
circuit board: 9.65cm x 6.35cm

parts:
  PRO_MINI = Arduino Pro Mini (3.3V)
  BAT_CHG = Micro Lipo Charger
  BLU = Bluetooth Mate Silver
  Oxi_header = female pin header, 4 pins [form="♀ (female)"]
  J2 = female pin header, 2 pins [form="♀ (female)"]
  J3 = female pin header, 6 pins [form="♀ (female)"]
  OLED_header = female pin header, 8 pins [form="♀ (female)"]
  J5 = Generic female header - 6 pins [form="♀ (female)" package=THT]

nets:
  N1: PRO_MINI.DTR, J5.DTR
  N2: PRO_MINI.TXO, J5.RXI
  N3: PRO_MINI.RXI, J5.TXO
  N4: PRO_MINI.VCC, Oxi_header.pin2
  GND: PRO_MINI.GND, BAT_CHG.GND, BLU.GND, Oxi_header.pin3, J3.pin1, OLED_header.pin8, J5.GND, J5.CTS
  N5: PRO_MINI.A4, Oxi_header.pin4
  N6: PRO_MINI.A5, Oxi_header.pin1
  5V: PRO_MINI.RAW, BAT_CHG.VBAT, BAT_CHG.5V, BLU.VCC, J3.pin3, OLED_header.pin7
  N7: PRO_MINI.SCK, OLED_header.pin4
  N8: PRO_MINI.MISO, OLED_header.pin5
  N9: PRO_MINI.MOSI, OLED_header.pin3
  N10: PRO_MINI.D10, OLED_header.pin2
  N11: PRO_MINI.D9, OLED_header.pin1
  N12: PRO_MINI.D2, J2.pin1
  N13: BLU.TX, J3.pin4
  N14: BLU.RX, J3.pin5

notes:
  by Andres Machado
  PD3D

custom parts:
  Micro Lipo Charger: Oh so handy, this little lipo charger is so small and easy to use you can keep it on your desk or mount it easily into any project! Simply plug it via any MicroUSB cable into a USB port and a 3.7V/4.2V lithium polymer or lithium ion rechargeable battery into the JST plug on the other end. There are two LEDs - one red and one green. While charging, the red LED is lit. When the battery is fully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
  Bluetooth Mate Silver: Description: The Bluetooth Mate is very similar to our BlueSMiRF modem, but it is designed specifically to be used with our Arduino Pros and LilyPad Arduinos. These modems work as a serial (RX/TX) pipe, and are a great wireless replacement for serial cables. Any serial stream from 9600 to 115200bps can be passed seamlessly from your computer to your target. Bluetooth Mate has the same pin out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
  Generic female header - 6 pins: Generic female header
